# Fritzing sketch Design (saved by Fritzing 0.9.3b)
circuit board: 8.46667cm x 5.64444cm
perfboards: 1

parts:
  Nokia_5110_LCD = Nokia 5110 LCD basado en PCD8544
  Left_Btn = Pushbutton [package="[THT]"]
  Red_Btn = Pushbutton [package="[THT]"]
  Right_Btn = Pushbutton [package="[THT]"]
  Green_Btn = Pushbutton [package="[THT]"]
  R1 = Resistor [tolerance=±5% resistance=10k package="0402 [SMD]"]
  R2 = Resistor [tolerance=±5% resistance=10k package="0402 [SMD]"]
  R3 = Resistor [tolerance=±5% resistance=10k package="0402 [SMD]"]
  R4 = Resistor [tolerance=±5% resistance=10k package="0402 [SMD]"]
  Componente1 = Arduino Uno (Rev3)

nets:
  VCC: Nokia_5110_LCD.VCC, Componente1.3V3
  GND: Nokia_5110_LCD.GND, R1.Pin_0, R2.Pin_1, R3.Pin_0, R4.Pin_1, Componente1.GND
  N1: Nokia_5110_LCD.CE, Componente1.D11_PWM/MOSI
  N2: Nokia_5110_LCD.RST, Componente1.D12/MISO
  N3: Nokia_5110_LCD.DC, Componente1.D10_PWM/SS
  N4: Nokia_5110_LCD.DIN, Componente1.D9_PWM
  N5: Nokia_5110_LCD.CLK, Componente1.D8
  N6: Nokia_5110_LCD.LIGHT, Componente1.D0/RX
  N7: Left_Btn.Pin_1, Left_Btn.Pin_2, R4.Pin_0, Componente1.D6_PWM
  N8: Left_Btn.Pin_3, Left_Btn.Pin_4, Red_Btn.Pin_1, Red_Btn.Pin_2, Right_Btn.Pin_1, Right_Btn.Pin_2, Green_Btn.Pin_3, Green_Btn.Pin_4, Componente1.5V
  N9: Red_Btn.Pin_3, Red_Btn.Pin_4, R2.Pin_0, Componente1.D5_PWM
  N10: Right_Btn.Pin_3, Right_Btn.Pin_4, R1.Pin_1, Componente1.D4
  N11: Green_Btn.Pin_1, Green_Btn.Pin_2, R3.Pin_1, Componente1.D3_PWM

custom parts:
  Nokia 5110 LCD basado en PCD8544: Módulo Nokia 5110 LCD basado en el controlador PCD8544. Versión de 8 pines (sólo entrada).
